# Fritzing sketch schematics (saved by Fritzing 0.9.3b)
breadboards: 1

parts:
  S1 = Pushbutton [package="[THT]"]
  S2 = Pushbutton [package="[THT]"]
  S3 = Pushbutton [package="[THT]"]
  Part1 = Arduino Uno (Rev3) - ICSP
  U1 = LCD-16X2 [package=lcd-16x2_noholes]
  R1 = TRIMPOT [package=trimpot_pth_s3_lock]
  R2 = Resistor [tolerance=±5% resistance=220 package="0603 [SMD]"]
  LED1 = RGB LED (com. cathode, rgb) [package="5 mm [THT]"]
  R3 = Resistor [tolerance=±5% resistance=220 package="1206 [SMD]"]
  R4 = Resistor [tolerance=±5% resistance=220 package="1206 [SMD]"]
  R5 = Resistor [tolerance=±5% resistance=220 package="1206 [SMD]"]
  Part2 = HC-SR501 Body Sensor Module
  S4 = Reed switch [package=THT]
  R6 = Photocell (LDR) [package=THT]
  R7 = Resistor [tolerance=±5% resistance=10k package=THT]
  U2 = TRANSISTOR_NPN_2 [package=to-92]
  R8 = Resistor [tolerance=±5% resistance=10k package=THT]
  Q1 = Basic FET P-Channel [package="DPak [SMD]"]
  R9 = Resistor [tolerance=±5% resistance=220 package="1206 [SMD]"]
  LED2 = LED - 5mm [color="Red (633nm)" package="5 mm [THT]"]
  M1 = DC Motor

nets:
  GND: S1.Pin_1, S1.Pin_2, S2.Pin_1, S2.Pin_2, S3.Pin_1, S3.Pin_2, Part1.GND, U1.VSS, U1.R_W, U1.K, R1.CCW, LED1.common_cathode, Part2.GND, S4.pin_1, R7.Pin_0, U2.C, Q1.source, M1.pin_1
  N1: S1.Pin_3, S1.Pin_4, Part1.D4
  N2: S2.Pin_3, S2.Pin_4, Part1.D3_PWM
  N3: S3.Pin_3, S3.Pin_4, Part1.D2
  N4: Part1.A0, Q1.Gate
  N5: Part1.A1, R6.pin_1, R7.Pin_1
  N6: Part1.A2, U1.DB7
  N7: Part1.A3, U1.DB6
  N8: Part1.A4/SDA, U1.DB5
  N9: Part1.A5/SCL, U1.DB4
  N10: Part1.D8, Part2.OUT
  N11: Part1.D9_PWM, R4.Pin_0
  N12: Part1.D10_PWM/SS, R3.Pin_0
  N13: Part1.D11_PWM/MOSI, R5.Pin_0
  N14: Part1.D5_PWM, U1.RS
  N15: Part1.D6_PWM, U1.E
  N16: Part1.D7, S4.pin_2
  5V: Part1.5V, U1.VDD, R1.CW, R2.Pin_0, Part2.VCC, R6.pin_0, U2.E, R8.Pin_1, R9.Pin_0
  N17: U1.VO, R1.WIPER
  N18: U1.A, R2.Pin_1
  N19: LED1.red_anode, R5.Pin_1
  N20: LED1.green_anode, R3.Pin_1
  N21: LED1.blue_anode, R4.Pin_1
  N22: U2.B, R8.Pin_0
  N23: Q1.drain, LED2.anode, M1.pin_2
  N24: R9.Pin_1, LED2.cathode

custom parts:
  HC-SR501 Body Sensor Module: Pyroelectric Infrared PIR Motion Sensor Detector Module
